# Fritzing sketch Prototipo_Nodemcu (saved by Fritzing 0.9.3b)
breadboards: 1

parts:
  T2 = LM35 Temperature Sensor [package="TO92 [THT]"]
  GY1 = GY-521 (MPU-6050) [form="♀ (female)" package=THT]
  U1 = NodeMCU V1.0

nets:
  VCC: T2.+Vs, GY1.VCC, U1.3V3
  N1: T2.Vout, U1.A0
  GND: T2.GND, GY1.GND, U1.GND
  N2: GY1.SCL, U1.D1
  N3: GY1.SDA, U1.D2

custom parts:
  GY-521 (MPU-6050): Placa GY-521 basada en conjunto de acelerómetro+giroscopios MPU-6050
  NodeMCU V1.0: ESP8266 based NodeMCU
